// Logisim project CSE332 PROJECT 17 Bit ALU.circ as structural Verilog: 4 circuits, main circuit 1bit ALU
// ALU
module _1bit_ALU (
  input  [1:0] Select_Bits,
  input  Cin,
  input  A,
  input  B,
  input  Cin_sub,
  output Output,
  output Cout,
  output Cout_sub
);

  wire divider_1_out, nand_1_out, subtractor_1_out, xor_1_out;

  Subtractor #(.width(1)) subtractor_1 (.a(A), .b(B), .out(subtractor_1_out), .bin(Cin), .bout(Cout));
  nand nand_1 (nand_1_out, A, B);
  xor xor_1 (xor_1_out, A, B);
  Divider #(.width(1)) divider_1 (.a(A), .b(B), .out(divider_1_out), .upper(Cin_sub), .rem(Cout_sub));
  Multiplexer #(.select(2)) multiplexer_1 (
    .in0(nand_1_out), .in1(xor_1_out), .in2(subtractor_1_out), .in3(divider_1_out), .out(Output),
    .sel(Select_Bits));  // open: en
endmodule

// ALU
module _17bit_ALU (
  input  in_1,
  input  [1:0] Select_bits,
  input  in_3,
  input  [16:0] A,
  input  [16:0] B,
  output [16:0] Output,
  output out_7,
  output out_8
);

  wire n1bit_alu_1_cout, n1bit_alu_1_cout_sub, n1bit_alu_2_cout, n1bit_alu_2_cout_sub, n1bit_alu_3_cout,
       n1bit_alu_3_cout_sub, n1bit_alu_4_cout, n1bit_alu_4_cout_sub, n1bit_alu_5_cout, n1bit_alu_5_cout_sub,
       n1bit_alu_6_cout, n1bit_alu_6_cout_sub, n1bit_alu_7_cout, n1bit_alu_7_cout_sub, n1bit_alu_8_cout,
       n1bit_alu_8_cout_sub, n1bit_alu_9_cout, n1bit_alu_9_cout_sub, n1bit_alu_10_cout,
       n1bit_alu_10_cout_sub, n1bit_alu_11_cout, n1bit_alu_11_cout_sub, n1bit_alu_12_cout,
       n1bit_alu_12_cout_sub, n1bit_alu_13_cout, n1bit_alu_13_cout_sub, n1bit_alu_14_cout,
       n1bit_alu_14_cout_sub, n1bit_alu_15_cout, n1bit_alu_15_cout_sub, n1bit_alu_16_cout,
       n1bit_alu_16_cout_sub;

  _1bit_ALU u_1bit_alu_1 (
    .A(A[0]), .B(B[0]), .Output(Output[0]), .Cin(in_1), .Cin_sub(in_3), .Select_Bits(Select_bits),
    .Cout(n1bit_alu_1_cout), .Cout_sub(n1bit_alu_1_cout_sub));
  _1bit_ALU u_1bit_alu_2 (
    .A(A[1]), .B(B[1]), .Output(Output[1]), .Cin(n1bit_alu_1_cout), .Cin_sub(n1bit_alu_1_cout_sub),
    .Select_Bits(Select_bits), .Cout(n1bit_alu_2_cout), .Cout_sub(n1bit_alu_2_cout_sub));
  _1bit_ALU u_1bit_alu_3 (
    .A(A[2]), .B(B[2]), .Output(Output[2]), .Cin(n1bit_alu_2_cout), .Cin_sub(n1bit_alu_2_cout_sub),
    .Select_Bits(Select_bits), .Cout(n1bit_alu_3_cout), .Cout_sub(n1bit_alu_3_cout_sub));
  _1bit_ALU u_1bit_alu_4 (
    .A(A[3]), .B(B[3]), .Output(Output[3]), .Cin(n1bit_alu_3_cout), .Cin_sub(n1bit_alu_3_cout_sub),
    .Select_Bits(Select_bits), .Cout(n1bit_alu_4_cout), .Cout_sub(n1bit_alu_4_cout_sub));
  _1bit_ALU u_1bit_alu_5 (
    .A(A[4]), .B(B[4]), .Output(Output[4]), .Cin(n1bit_alu_4_cout), .Cin_sub(n1bit_alu_4_cout_sub),
    .Select_Bits(Select_bits), .Cout(n1bit_alu_5_cout), .Cout_sub(n1bit_alu_5_cout_sub));
  _1bit_ALU u_1bit_alu_6 (
    .A(A[5]), .B(B[5]), .Output(Output[5]), .Cin(n1bit_alu_5_cout), .Cin_sub(n1bit_alu_5_cout_sub),
    .Select_Bits(Select_bits), .Cout(n1bit_alu_6_cout), .Cout_sub(n1bit_alu_6_cout_sub));
  _1bit_ALU u_1bit_alu_7 (
    .A(A[6]), .B(B[6]), .Output(Output[6]), .Cin(n1bit_alu_6_cout), .Cin_sub(n1bit_alu_6_cout_sub),
    .Select_Bits(Select_bits), .Cout(n1bit_alu_7_cout), .Cout_sub(n1bit_alu_7_cout_sub));
  _1bit_ALU u_1bit_alu_8 (
    .A(A[7]), .B(B[7]), .Output(Output[7]), .Cin(n1bit_alu_7_cout), .Cin_sub(n1bit_alu_7_cout_sub),
    .Select_Bits(Select_bits), .Cout(n1bit_alu_8_cout), .Cout_sub(n1bit_alu_8_cout_sub));
  _1bit_ALU u_1bit_alu_9 (
    .A(A[8]), .B(B[8]), .Output(Output[8]), .Cin(n1bit_alu_8_cout), .Cin_sub(n1bit_alu_8_cout_sub),
    .Select_Bits(Select_bits), .Cout(n1bit_alu_9_cout), .Cout_sub(n1bit_alu_9_cout_sub));
  _1bit_ALU u_1bit_alu_10 (
    .A(A[9]), .B(B[9]), .Output(Output[9]), .Cin(n1bit_alu_9_cout), .Cin_sub(n1bit_alu_9_cout_sub),
    .Select_Bits(Select_bits), .Cout(n1bit_alu_10_cout), .Cout_sub(n1bit_alu_10_cout_sub));
  _1bit_ALU u_1bit_alu_11 (
    .A(A[10]), .B(B[10]), .Output(Output[10]), .Cin(n1bit_alu_10_cout), .Cin_sub(n1bit_alu_10_cout_sub),
    .Select_Bits(Select_bits), .Cout(n1bit_alu_11_cout), .Cout_sub(n1bit_alu_11_cout_sub));
  _1bit_ALU u_1bit_alu_12 (
    .A(A[11]), .B(B[11]), .Output(Output[11]), .Cin(n1bit_alu_11_cout), .Cin_sub(n1bit_alu_11_cout_sub),
    .Select_Bits(Select_bits), .Cout(n1bit_alu_12_cout), .Cout_sub(n1bit_alu_12_cout_sub));
  _1bit_ALU u_1bit_alu_13 (
    .A(A[12]), .B(B[12]), .Output(Output[12]), .Cin(n1bit_alu_12_cout), .Cin_sub(n1bit_alu_12_cout_sub),
    .Select_Bits(Select_bits), .Cout(n1bit_alu_13_cout), .Cout_sub(n1bit_alu_13_cout_sub));
  _1bit_ALU u_1bit_alu_14 (
    .A(A[13]), .B(B[13]), .Output(Output[13]), .Cin(n1bit_alu_13_cout), .Cin_sub(n1bit_alu_13_cout_sub),
    .Select_Bits(Select_bits), .Cout(n1bit_alu_14_cout), .Cout_sub(n1bit_alu_14_cout_sub));
  _1bit_ALU u_1bit_alu_15 (
    .A(A[14]), .B(B[14]), .Output(Output[14]), .Cin(n1bit_alu_14_cout), .Cin_sub(n1bit_alu_14_cout_sub),
    .Select_Bits(Select_bits), .Cout(n1bit_alu_15_cout), .Cout_sub(n1bit_alu_15_cout_sub));
  _1bit_ALU u_1bit_alu_16 (
    .A(A[15]), .B(B[15]), .Output(Output[15]), .Cin(n1bit_alu_15_cout), .Cin_sub(n1bit_alu_15_cout_sub),
    .Select_Bits(Select_bits), .Cout(n1bit_alu_16_cout), .Cout_sub(n1bit_alu_16_cout_sub));
  _1bit_ALU u_1bit_alu_17 (
    .A(A[16]), .B(B[16]), .Output(Output[16]), .Cin(n1bit_alu_16_cout), .Cin_sub(n1bit_alu_16_cout_sub),
    .Select_Bits(Select_bits), .Cout(out_8), .Cout_sub(out_7));
endmodule

// 8 bit Multiplier
module _8into8_multiplier (
  input  [7:0] A,
  input  [7:0] B,
  input  in_3,
  output [16:0] out_4
);

  wire adder_1_cout, adder_1_out, adder_2_cout, adder_2_out, adder_3_cout, adder_3_out, adder_4_cout,
       adder_5_cout, adder_5_out, adder_6_cout, adder_6_out, adder_7_cout, adder_7_out, adder_8_cout,
       adder_8_out, adder_9_cout, adder_9_out, adder_10_cout, adder_10_out, adder_11_cout, adder_11_out,
       adder_12_cout, adder_12_out, adder_13_cout, adder_13_out, adder_14_cout, adder_15_cout, adder_15_out,
       adder_16_cout, adder_17_cout, adder_17_out, adder_18_cout, adder_18_out, adder_19_cout, adder_19_out,
       adder_20_cout, adder_20_out, adder_21_cout, adder_21_out, adder_22_cout, adder_22_out, adder_23_cout,
       adder_23_out, adder_24_cout, adder_24_out, adder_25_cout, adder_25_out, adder_26_cout, adder_26_out,
       adder_27_cout, adder_28_cout, adder_28_out, adder_29_cout, adder_30_cout, adder_30_out, adder_31_cout,
       adder_31_out, adder_32_cout, adder_32_out, adder_33_cout, adder_33_out, adder_34_cout, adder_34_out,
       adder_35_cout, adder_35_out, adder_36_cout, adder_36_out, adder_37_cout, adder_37_out, adder_38_cout,
       adder_40_cout, adder_41_cout, adder_42_cout, adder_42_out, adder_43_cout, adder_43_out, adder_44_cout,
       adder_44_out, adder_45_cout, adder_45_out, adder_46_cout, adder_46_out, adder_47_cout, adder_48_cout,
       adder_48_out, adder_49_cout, adder_50_cout, adder_51_cout, adder_52_cout, and_2_out, and_3_out,
       and_4_out, and_5_out, and_6_out, and_7_out, and_8_out, and_9_out, and_10_out, and_11_out, and_12_out,
       and_13_out, and_14_out, and_15_out, and_16_out, and_17_out, and_18_out, and_19_out, and_20_out,
       and_21_out, and_22_out, and_23_out, and_24_out, and_25_out, and_26_out, and_27_out, and_28_out,
       and_29_out, and_30_out, and_31_out, and_32_out, and_33_out, and_34_out, and_35_out, and_36_out,
       and_37_out, and_38_out, and_39_out, and_40_out, and_41_out, and_42_out, and_43_out, and_44_out,
       and_45_out, and_46_out, and_47_out, and_48_out, and_49_out, and_50_out, and_51_out, and_52_out,
       and_53_out, and_54_out, and_55_out, and_56_out, and_57_out, and_58_out, and_59_out, and_60_out,
       and_61_out, and_63_out, and_64_out, and_65_out, and_66_out, and_67_out, and_68_out;

  and and_1 (out_4[1], A[0], B[0]);
  and and_2 (and_2_out, A[1], B[0]);
  and and_3 (and_3_out, A[1], B[1]);
  and and_4 (and_4_out, A[2], B[0]);
  and and_5 (and_5_out, A[1], B[1]);
  and and_6 (and_6_out, A[0], B[2]);
  and and_7 (and_7_out, A[3], B[0]);
  and and_8 (and_8_out, A[3], B[0]);
  and and_9 (and_9_out, A[2], B[1]);
  and and_10 (and_10_out, A[1], B[2]);
  and and_11 (and_11_out, A[4], B[0]);
  and and_12 (and_12_out, A[3], B[1]);
  and and_13 (and_13_out, A[2], B[2]);
  and and_14 (and_14_out, A[1], B[3]);
  and and_15 (and_15_out, A[0], B[4]);
  and and_16 (and_16_out, A[5], B[0]);
  and and_17 (and_17_out, A[4], B[1]);
  and and_18 (and_18_out, A[3], B[2]);
  and and_19 (and_19_out, A[2], B[3]);
  and and_20 (and_20_out, A[1], B[4]);
  and and_21 (and_21_out, A[0], B[5]);
  and and_22 (and_22_out, A[6], B[0]);
  and and_23 (and_23_out, A[5], B[1]);
  and and_24 (and_24_out, A[4], B[2]);
  and and_25 (and_25_out, A[3], B[3]);
  and and_26 (and_26_out, A[2], B[4]);
  and and_27 (and_27_out, A[1], B[5]);
  and and_28 (and_28_out, A[0], B[6]);
  and and_29 (and_29_out, A[7], B[0]);
  and and_30 (and_30_out, A[6], B[1]);
  and and_31 (and_31_out, A[5], B[2]);
  and and_32 (and_32_out, A[4], B[3]);
  and and_33 (and_33_out, A[3], B[4]);
  and and_34 (and_34_out, A[2], B[5]);
  and and_35 (and_35_out, A[1], B[6]);
  and and_36 (and_36_out, A[0], B[7]);
  and and_37 (and_37_out, A[7], B[1]);
  and and_38 (and_38_out, A[6], B[2]);
  and and_39 (and_39_out, A[5], B[3]);
  and and_40 (and_40_out, A[4], B[4]);
  and and_41 (and_41_out, A[3], B[5]);
  and and_42 (and_42_out, A[7], B[2]);
  and and_43 (and_43_out, A[6], B[3]);
  and and_44 (and_44_out, A[5], B[4]);
  and and_45 (and_45_out, A[7], B[4]);
  and and_46 (and_46_out, A[7], B[3]);
  and and_47 (and_47_out, A[6], B[4]);
  and and_48 (and_48_out, A[5], B[5]);
  and and_49 (and_49_out, A[6], B[7]);
  and and_50 (and_50_out, A[7], B[6]);
  and and_51 (and_51_out, A[7], B[4]);
  and and_52 (and_52_out, A[6], B[5]);
  and and_53 (and_53_out, A[5], B[6]);
  and and_54 (and_54_out, A[4], B[7]);
  Adder #(.width(1)) adder_1 (
    .a(and_7_out), .b(and_8_out), .out(adder_1_out), .cin(adder_16_cout), .cout(adder_1_cout));
  Adder #(.width(1)) adder_2 (
    .a(and_29_out), .b(and_30_out), .out(adder_2_out), .cin(adder_49_cout), .cout(adder_2_cout));
  Adder #(.width(1)) adder_3 (
    .a(and_51_out), .b(and_52_out), .out(adder_3_out), .cin(adder_14_cout), .cout(adder_3_cout));
  Adder #(.width(1)) adder_4 (.a(and_2_out), .b(and_3_out), .out(out_4[2]), .cin(in_3), .cout(adder_4_cout));
  Adder #(.width(1)) adder_5 (.a(and_4_out), .b(and_5_out), .out(adder_5_out), .cin(adder_4_cout), .cout(adder_5_cout));
  Adder #(.width(1)) adder_6 (
    .a(adder_1_out), .b(and_9_out), .out(adder_6_out), .cin(adder_1_cout), .cout(adder_6_cout));
  and and_55 (and_55_out, A[0], B[3]);
  Adder #(.width(1)) adder_7 (
    .a(and_11_out), .b(and_12_out), .out(adder_7_out), .cin(adder_29_cout), .cout(adder_7_cout));
  Adder #(.width(1)) adder_8 (
    .a(and_16_out), .b(and_17_out), .out(adder_8_out), .cin(adder_40_cout), .cout(adder_8_cout));
  Adder #(.width(1)) adder_9 (
    .a(and_22_out), .b(and_23_out), .out(adder_9_out), .cin(adder_41_cout), .cout(adder_9_cout));
  Adder #(.width(1)) adder_10 (
    .a(adder_2_out), .b(and_31_out), .out(adder_10_out), .cin(adder_2_cout), .cout(adder_10_cout));
  Adder #(.width(1)) adder_11 (
    .a(and_37_out), .b(and_38_out), .out(adder_11_out), .cin(adder_50_cout), .cout(adder_11_cout));
  Adder #(.width(1)) adder_12 (
    .a(and_42_out), .b(and_43_out), .out(adder_12_out), .cin(adder_51_cout), .cout(adder_12_cout));
  Adder #(.width(1)) adder_13 (
    .a(and_46_out), .b(and_47_out), .out(adder_13_out), .cin(adder_52_cout), .cout(adder_13_cout));
  Adder #(.width(1)) adder_14 (
    .a(and_49_out), .b(and_50_out), .out(out_4[12]), .cin(adder_47_cout), .cout(adder_14_cout));
  Adder #(.width(1)) adder_15 (
    .a(adder_3_out), .b(and_53_out), .out(adder_15_out), .cin(adder_3_cout), .cout(adder_15_cout));
  and and_56 (and_56_out, A[7], B[5]);
  and and_57 (and_57_out, A[6], B[6]);
  and and_58 (and_58_out, A[5], B[7]);
  and and_59 (and_59_out, A[7], B[7]);
  and and_60 (and_60_out, A[6], B[7]);
  Adder #(.width(1)) adder_16 (
    .a(adder_5_out), .b(and_6_out), .out(out_4[3]), .cin(adder_5_cout), .cout(adder_16_cout));
  Adder #(.width(1)) adder_17 (
    .a(adder_6_out), .b(and_10_out), .out(adder_17_out), .cin(adder_6_cout), .cout(adder_17_cout));
  Adder #(.width(1)) adder_18 (
    .a(adder_7_out), .b(and_13_out), .out(adder_18_out), .cin(adder_7_cout), .cout(adder_18_cout));
  Adder #(.width(1)) adder_19 (
    .a(adder_8_out), .b(and_18_out), .out(adder_19_out), .cin(adder_8_cout), .cout(adder_19_cout));
  Adder #(.width(1)) adder_20 (
    .a(adder_9_out), .b(and_24_out), .out(adder_20_out), .cin(adder_9_cout), .cout(adder_20_cout));
  Adder #(.width(1)) adder_21 (
    .a(adder_10_out), .b(and_32_out), .out(adder_21_out), .cin(adder_10_cout), .cout(adder_21_cout));
  Adder #(.width(1)) adder_22 (
    .a(adder_11_out), .b(and_39_out), .out(adder_22_out), .cin(adder_11_cout), .cout(adder_22_cout));
  Adder #(.width(1)) adder_23 (
    .a(adder_22_out), .b(and_40_out), .out(adder_23_out), .cin(adder_22_cout), .cout(adder_23_cout));
  Adder #(.width(1)) adder_24 (
    .a(adder_12_out), .b(and_44_out), .out(adder_24_out), .cin(adder_12_cout), .cout(adder_24_cout));
  Adder #(.width(1)) adder_25 (
    .a(adder_24_out), .b(and_45_out), .out(adder_25_out), .cin(adder_24_cout), .cout(adder_25_cout));
  Adder #(.width(1)) adder_26 (
    .a(adder_13_out), .b(and_48_out), .out(adder_26_out), .cin(adder_13_cout), .cout(adder_26_cout));
  and and_61 (and_61_out, A[4], B[6]);
  Adder #(.width(1)) adder_27 (
    .a(adder_15_out), .b(and_54_out), .out(out_4[13]), .cin(adder_15_cout), .cout(adder_27_cout));
  Adder #(.width(1)) adder_28 (
    .a(and_56_out), .b(and_57_out), .out(adder_28_out), .cin(adder_27_cout), .cout(adder_28_cout));
  and and_62 (out_4[16], A[7], B[7]);
  Adder #(.width(1)) adder_29 (
    .a(adder_17_out), .b(and_55_out), .out(out_4[4]), .cin(adder_17_cout), .cout(adder_29_cout));
  Adder #(.width(1)) adder_30 (
    .a(adder_18_out), .b(and_14_out), .out(adder_30_out), .cin(adder_18_cout), .cout(adder_30_cout));
  Adder #(.width(1)) adder_31 (
    .a(adder_19_out), .b(and_19_out), .out(adder_31_out), .cin(adder_19_cout), .cout(adder_31_cout));
  Adder #(.width(1)) adder_32 (
    .a(adder_31_out), .b(and_20_out), .out(adder_32_out), .cin(adder_31_cout), .cout(adder_32_cout));
  Adder #(.width(1)) adder_33 (
    .a(adder_20_out), .b(and_25_out), .out(adder_33_out), .cin(adder_20_cout), .cout(adder_33_cout));
  Adder #(.width(1)) adder_34 (
    .a(adder_21_out), .b(and_33_out), .out(adder_34_out), .cin(adder_21_cout), .cout(adder_34_cout));
  Adder #(.width(1)) adder_35 (
    .a(adder_23_out), .b(and_41_out), .out(adder_35_out), .cin(adder_23_cout), .cout(adder_35_cout));
  and and_63 (and_63_out, A[2], B[6]);
  Adder #(.width(1)) adder_36 (
    .a(adder_25_out), .b(and_64_out), .out(adder_36_out), .cin(adder_25_cout), .cout(adder_36_cout));
  and and_64 (and_64_out, A[4], B[5]);
  Adder #(.width(1)) adder_37 (
    .a(adder_26_out), .b(and_61_out), .out(adder_37_out), .cin(adder_26_cout), .cout(adder_37_cout));
  Adder #(.width(1)) adder_38 (
    .a(adder_28_out), .b(and_58_out), .out(out_4[14]), .cin(adder_28_cout), .cout(adder_38_cout));
  Adder #(.width(1)) adder_39 (.a(and_59_out), .b(and_60_out), .out(out_4[15]), .cin(adder_38_cout), .cout(out_4[0]));
  Adder #(.width(1)) adder_40 (
    .a(adder_30_out), .b(and_15_out), .out(out_4[5]), .cin(adder_30_cout), .cout(adder_40_cout));
  Adder #(.width(1)) adder_41 (
    .a(adder_32_out), .b(and_21_out), .out(out_4[6]), .cin(adder_32_cout), .cout(adder_41_cout));
  Adder #(.width(1)) adder_42 (
    .a(adder_33_out), .b(and_26_out), .out(adder_42_out), .cin(adder_33_cout), .cout(adder_42_cout));
  Adder #(.width(1)) adder_43 (
    .a(adder_34_out), .b(and_34_out), .out(adder_43_out), .cin(adder_34_cout), .cout(adder_43_cout));
  Adder #(.width(1)) adder_44 (
    .a(adder_43_out), .b(and_35_out), .out(adder_44_out), .cin(adder_43_cout), .cout(adder_44_cout));
  Adder #(.width(1)) adder_45 (
    .a(adder_35_out), .b(and_63_out), .out(adder_45_out), .cin(adder_35_cout), .cout(adder_45_cout));
  and and_65 (and_65_out, A[1], A[7]);
  Adder #(.width(1)) adder_46 (
    .a(adder_36_out), .b(and_66_out), .out(adder_46_out), .cin(adder_36_cout), .cout(adder_46_cout));
  and and_66 (and_66_out, A[3], B[6]);
  Adder #(.width(1)) adder_47 (
    .a(adder_37_out), .b(and_67_out), .out(out_4[11]), .cin(adder_37_cout), .cout(adder_47_cout));
  and and_67 (and_67_out, A[3], B[7]);
  Adder #(.width(1)) adder_48 (
    .a(adder_42_out), .b(and_27_out), .out(adder_48_out), .cin(adder_42_cout), .cout(adder_48_cout));
  Adder #(.width(1)) adder_49 (
    .a(adder_48_out), .b(and_28_out), .out(out_4[7]), .cin(adder_48_cout), .cout(adder_49_cout));
  Adder #(.width(1)) adder_50 (
    .a(adder_44_out), .b(and_36_out), .out(out_4[8]), .cin(adder_44_cout), .cout(adder_50_cout));
  Adder #(.width(1)) adder_51 (
    .a(adder_45_out), .b(and_65_out), .out(out_4[9]), .cin(adder_45_cout), .cout(adder_51_cout));
  Adder #(.width(1)) adder_52 (
    .a(adder_46_out), .b(and_68_out), .out(out_4[10]), .cin(adder_46_cout), .cout(adder_52_cout));
  and and_68 (and_68_out, A[2], B[7]);
endmodule

module Main (
  input  [16:0] A,
  input  [16:0] B,
  input  in_3,
  input  [1:0] in_4,
  input  [1:0] in_5,
  output [16:0] out_6,
  output [7:0] out_7,
  output [7:0] out_8
);

  wire [16:0] n8into8_multiplier_1_out_4, n17bit_alu_1_output;

  BitSelector #(.width(17), .group(8)) bitselector_1 (.in(A), .out(out_7), .sel(in_4));
  BitSelector #(.width(17), .group(8)) bitselector_2 (.in(B), .out(out_8), .sel(in_5));
  _17bit_ALU u_17bit_alu_1 (.A(A), .B(B), .Output(n17bit_alu_1_output));  // open: in_1, in_3, out_7, Select_bits, out_8
  _8into8_multiplier u_8into8_multiplier_1 (.A(out_7), .B(out_8), .out_4(n8into8_multiplier_1_out_4));  // open: in_3
  Multiplexer #(.width(17), .enable("false")) multiplexer_1 (
    .in0(n17bit_alu_1_output), .in1(n8into8_multiplier_1_out_4), .out(out_6), .sel(in_3));
endmodule
